# Fritzing sketch wifiRelaisFritzing (saved by Fritzing 0.9.3b)
breadboards: 1

parts:
  U1 = NodeMCU V3.0
  KY-1 = Keyes Relay [package=THT]
  HLK-PM1 = HLK-PM01
  LED1 = LED - 5mm [color="Red (633nm)" package="5 mm [THT]"]
  Q1 = PNP-Transistor [package="TO92 [THT]"]
  R2 = Resistor [tolerance=±5% resistance=220 package=THT]
  R3 = Resistor [tolerance=±5% resistance=220 package=THT]
  S2 = Taiway 100-SP-X-T1 SPDT Miniature Toggle Switch [part_number=100-SP-X-T1-0-0-B1-M1 package=THT]

nets:
  N1: U1.D0, S2.L1
  N2: U1.D1, LED1.cathode
  N3: U1.D2, R2.Pin_0
  N4: U1.GND#6, U1.GND#13, U1.GND#16, U1.GND#33, KY-1.ground, HLK-PM1.-Vo, Q1.C, R3.Pin_1, S2.L2
  N5: U1.Vin, KY-1.power, HLK-PM1.+Vo
  N6: KY-1.signal, Q1.E
  N7: LED1.anode, R3.Pin_0
  N8: Q1.B, R2.Pin_1

notes:
  230V, AC
  ground
  hot
  neutral

custom parts:
  NodeMCU V3.0: ESP8266 based NodeMCU
  Keyes Relay: The Keyes 5V relay module is suitable for SCM development, home appliance control. It uses a 5V~12V TIL control signal which can control DC / AC signal.
